// Logisim project CPU.circ as structural Verilog: 17 circuits, main circuit OCTALBUSTRANSCEIVER
module main (
  input  CLEAR,
  input  LOAD,
  input  ENA,
  input  Select,
  input  Pulse,
  input  Hlt,
  input  [3:0] BUSADD,
  input  CLEAR_2,
  input  LOAD_2,
  input  PROGRAMMING,
  input  RESET,
  input  CS,
  input  SU,
  input  E0,
  input  S2,
  input  S1,
  input  ENA_2,
  input  WR,
  input  CLEAR_3,
  input  LOAD_3,
  input  CO,
  input  ENA_3,
  input  CLEAR_4,
  input  LOAD_4,
  input  LOAD_5,
  input  CE,
  input  RESET_2,
  input  D8,
  input  D7,
  input  D6,
  input  D5,
  input  D4,
  input  D3,
  input  D2,
  input  D1,
  output Carry
);

  wire and_1_out, and_2_out, and_3_out, and_4_out, CLOCK_output, MANUALWRITE_out, not_1_out, not_2_out,
       not_3_out, not_4_out, not_5_out, not_6_out, or_1_out, or_2_out;
  wire [3:0] ADD_MUX_out, COUNTER_q0, MANUALADDRESS_sw4, MANUALDATA_sw4, MANUALDATA_sw8, MEM_REG_q,
       octalbustransceiver_1_q, octalbustransceiver_1_q_2;
  wire [7:0] ADD_MUX_3_out, IREG_q, RAM_o, REG_A_q, REG_B_q;

  not not_1 (not_1_out, CS);
  and and_1 (and_1_out, PROGRAMMING, MANUALWRITE_out);
  or or_1 (or_1_out, not_1_out, or_2_out);
  DipSwitch #(.number(4)) MANUALADDRESS (
    .sw1(MANUALADDRESS_sw4[3]), .sw2(MANUALADDRESS_sw4[2]), .sw3(MANUALADDRESS_sw4[1]),
    .sw4(MANUALADDRESS_sw4[0]));
  or or_2 (or_2_out, and_1_out, and_2_out);
  Button MANUALWRITE (.out(MANUALWRITE_out));
  MEMREG4BIT MEM_REG (.CLEAR(CLEAR), .LOAD(LOAD), .D(BUSADD), .CLOCK(CLOCK_output), .Q(MEM_REG_q));
  RAM16BYTE RAM (.A(ADD_MUX_out), .RESET(RESET), .D(ADD_MUX_3_out), .WR(or_2_out), .CS(CS), .O(RAM_o));
  and and_2 (and_2_out, CLOCK_output, WR);
  DipSwitch MANUALDATA (
    .sw1(MANUALDATA_sw4[3]), .sw2(MANUALDATA_sw4[2]), .sw3(MANUALDATA_sw4[1]), .sw4(MANUALDATA_sw4[0]),
    .sw5(MANUALDATA_sw8[3]), .sw6(MANUALDATA_sw8[2]), .sw7(MANUALDATA_sw8[1]), .sw8(MANUALDATA_sw8[0]));
  DREG8BIT IREG (.CLEAR(CLEAR_4), .LOAD(LOAD_4), .CLOCK(CLOCK_output), .Q(IREG_q));  // open: D
  MUX2X1 ADD_MUX (.A(MANUALADDRESS_sw4), .B(MEM_REG_q), .Select(PROGRAMMING), .Out(ADD_MUX_out));
  not not_2 (not_2_out, or_2_out);
  LED led_1 (.in(RAM_o[6]));
  LED led_2 (.in(RAM_o[4]));
  LED led_3 (.in(RAM_o[5]));
  LED led_4 (.in(RAM_o[7]));
  LED led_5 (.in(IREG_q[4]));
  LED led_6 (.in(IREG_q[6]));
  LED led_7 (.in(IREG_q[5]));
  LED led_8 (.in(IREG_q[7]));
  LED led_9 (.in(ADD_MUX_out[2]));
  LED led_10 (.in(ADD_MUX_out[1]));
  LED led_11 (.in(ADD_MUX_out[3]));
  and and_3 (and_3_out, not_2_out, CS);
  LED led_12 (.in(RAM_o[3]));
  LED led_13 (.in(RAM_o[2]));
  LED led_14 (.in(RAM_o[1]));
  LED led_15 (.in(RAM_o[0]));
  LED led_16 (.in(IREG_q[0]));
  LED led_17 (.in(IREG_q[3]));
  LED led_18 (.in(IREG_q[1]));
  LED led_19 (.in(IREG_q[2]));
  LED led_20 (.in(ADD_MUX_out[0]));
  OCTALBUSTRANSCEIVER octalbustransceiver_1 (
    .D(RAM_o), .ENA(and_3_out), .Q({octalbustransceiver_1_q, octalbustransceiver_1_q_2}));
  MUX2X1 ADD_MUX_2 (.A(MANUALDATA_sw4), .B(octalbustransceiver_1_q), .Select(PROGRAMMING), .Out(ADD_MUX_3_out[7:4]));
  MUX2X1 ADD_MUX_3 (.A(MANUALDATA_sw8), .B(octalbustransceiver_1_q_2), .Select(PROGRAMMING), .Out(ADD_MUX_3_out[3:0]));
  OCTALBUSTRANSCEIVER octalbustransceiver_2 (
    .D(IREG_q), .ENA(ENA_3), .Q({octalbustransceiver_1_q, octalbustransceiver_1_q_2}));
  LED led_21 (.in(octalbustransceiver_1_q[3]));
  LED led_22 (.in(octalbustransceiver_1_q[1]));
  LED led_23 (.in(octalbustransceiver_1_q[2]));
  LED led_24 (.in(octalbustransceiver_1_q[0]));
  not not_3 (not_3_out, ENA_3);
  OCTALBUSTRANSCEIVER octalbustransceiver_3 (
    .D({D8, D7, D6, D5, D4, D3, D2, D1}), .ENA(and_4_out),
    .Q({octalbustransceiver_1_q, octalbustransceiver_1_q_2}));
  LED led_25 (.in(octalbustransceiver_1_q_2[1]));
  LED led_26 (.in(octalbustransceiver_1_q_2[3]));
  LED led_27 (.in(octalbustransceiver_1_q_2[0]));
  LED led_28 (.in(octalbustransceiver_1_q_2[2]));
  and and_4 (and_4_out, or_1_out, not_3_out, not_5_out, not_6_out, not_4_out, ~CO);  // AND_Gate
  TIMER CLOCK (.Select(Select), .Pulse(Pulse), .Hlt(Hlt), .Output(CLOCK_output));
  LED led_29 (.in(CLOCK_output));
  ALU ALU (
    .A(REG_A_q), .B(REG_B_q), .SU(SU), .S2(S2), .S1(S1), .E0(E0), .Carry(Carry),
    .Result({octalbustransceiver_1_q, octalbustransceiver_1_q_2}));
  not not_4 (not_4_out, E0);
  COUNTER4BIT COUNTER (
    .LOAD(LOAD_5), .ENA(CE), .CLK(CLOCK_output), .RESET(RESET_2), .D0(octalbustransceiver_1_q_2[0]),
    .Q0(COUNTER_q0[0]), .D1(octalbustransceiver_1_q_2[1]), .Q1(COUNTER_q0[1]),
    .D2(octalbustransceiver_1_q_2[2]), .Q2(COUNTER_q0[2]), .D3(octalbustransceiver_1_q_2[3]),
    .Q3(COUNTER_q0[3]));
  LED led_30 (.in(COUNTER_q0[3]));
  LED led_31 (.in(COUNTER_q0[0]));
  LED led_32 (.in(COUNTER_q0[1]));
  LED led_33 (.in(COUNTER_q0[2]));
  DREG8BIT REG_B (
    .CLEAR(CLEAR_2), .LOAD(LOAD_2), .D({octalbustransceiver_1_q, octalbustransceiver_1_q_2}),
    .CLOCK(CLOCK_output), .Q(REG_B_q));
  LED led_34 (.in(REG_A_q[7]));
  DREG8BIT REG_A (
    .CLEAR(CLEAR_3), .LOAD(LOAD_3), .D({octalbustransceiver_1_q, octalbustransceiver_1_q_2}),
    .CLOCK(CLOCK_output), .Q(REG_A_q));
  LED led_35 (.in(REG_B_q[4]));
  LED led_36 (.in(REG_B_q[7]));
  LED led_37 (.in(REG_B_q[6]));
  LED led_38 (.in(REG_B_q[5]));
  LED led_39 (.in(REG_A_q[4]));
  LED led_40 (.in(REG_A_q[5]));
  LED led_41 (.in(REG_A_q[3]));
  LED led_42 (.in(REG_A_q[6]));
  QUATERNARYTRANSCEIVER quaternarytransceiver_1 (.D(COUNTER_q0), .ENA(CO), .Q(octalbustransceiver_1_q_2));
  LED led_43 (.in(REG_B_q[0]));
  LED led_44 (.in(REG_B_q[1]));
  LED led_45 (.in(REG_B_q[3]));
  LED led_46 (.in(REG_B_q[2]));
  LED led_47 (.in(REG_A_q[0]));
  LED led_48 (.in(REG_A_q[2]));
  LED led_49 (.in(REG_A_q[1]));
  OCTALBUSTRANSCEIVER octalbustransceiver_4 (
    .D(REG_B_q), .ENA(ENA), .Q({octalbustransceiver_1_q, octalbustransceiver_1_q_2}));
  OCTALBUSTRANSCEIVER octalbustransceiver_5 (
    .D(REG_A_q), .ENA(ENA_2), .Q({octalbustransceiver_1_q, octalbustransceiver_1_q_2}));
  not not_5 (not_5_out, ENA);
  not not_6 (not_6_out, ENA_2);
endmodule

module TIMER (
  input  Select,
  input  Pulse,
  input  Hlt,
  output Output
);

  wire and_1_out, and_2_out, clock_1_out, not_1_out, not_2_out, or_1_out;

  Clock clock_1 (.out(clock_1_out));
  not not_1 (not_1_out, Select);
  and and_1 (and_1_out, clock_1_out, not_1_out);
  and and_2 (and_2_out, Select, Pulse);
  or or_1 (or_1_out, and_1_out, and_2_out);
  and and_3 (Output, or_1_out, not_2_out);
  not not_2 (not_2_out, Hlt);
endmodule

module DREG8BIT (
  input  CLEAR,
  input  LOAD,
  input  [7:0] D,
  input  CLOCK,
  output [7:0] Q
);

  wire and_1_out, and_2_out, and_3_out, and_4_out, and_5_out, and_6_out, and_7_out, and_8_out, and_9_out,
       and_10_out, and_11_out, and_12_out, and_13_out, and_14_out, and_15_out, and_16_out, d_ff_3_q,
       d_ff_3_qn, d_ff_5_q, d_ff_5_qn, d_ff_9_q, d_ff_9_qn, d_ff_11_q, d_ff_11_qn, not_1_out, not_2_out,
       not_3_out, not_4_out, not_5_out, not_6_out, not_7_out, not_8_out, or_1_out, or_2_out, or_3_out,
       or_4_out, or_5_out, or_6_out, or_7_out, or_8_out, undriven, undriven_2, undriven_3, undriven_4,
       undriven_5, undriven_6, undriven_7, undriven_8, undriven_9, undriven_10, undriven_11, undriven_12,
       undriven_13, undriven_14, undriven_15, undriven_16;

  not not_1 (not_1_out, LOAD);
  not not_2 (not_2_out, LOAD);
  not not_3 (not_3_out, LOAD);
  not not_4 (not_4_out, LOAD);
  not not_5 (not_5_out, LOAD);
  not not_6 (not_6_out, LOAD);
  not not_7 (not_7_out, LOAD);
  not not_8 (not_8_out, LOAD);
  and and_1 (and_1_out, Q[0], not_1_out);
  and and_2 (and_2_out, LOAD, D[0]);
  and and_3 (and_3_out, Q[1], not_2_out);
  and and_4 (and_4_out, LOAD, D[1]);
  and and_5 (and_5_out, Q[2], not_3_out);
  and and_6 (and_6_out, LOAD, D[2]);
  and and_7 (and_7_out, Q[3], not_4_out);
  and and_8 (and_8_out, LOAD, D[3]);
  and and_9 (and_9_out, Q[4], not_5_out);
  and and_10 (and_10_out, LOAD, D[4]);
  and and_11 (and_11_out, Q[5], not_6_out);
  and and_12 (and_12_out, LOAD, D[5]);
  and and_13 (and_13_out, Q[6], not_7_out);
  and and_14 (and_14_out, LOAD, D[6]);
  and and_15 (and_15_out, Q[7], not_8_out);
  and and_16 (and_16_out, LOAD, D[7]);
  D_Flip_Flop d_ff_1 (.D(or_1_out), .clk(CLOCK), .Q(Q[0]), .reset(CLEAR));  // open: Qn, preset
  or or_1 (or_1_out, and_1_out, and_2_out);
  D_Flip_Flop d_ff_2 (.D(or_2_out), .clk(CLOCK), .Q(Q[1]), .reset(CLEAR));  // open: Qn, preset
  or or_2 (or_2_out, and_3_out, and_4_out);
  D_Flip_Flop d_ff_3 (
    .clk(undriven), .D(undriven_2), .Q(d_ff_3_q), .Qn(d_ff_3_qn), .preset(undriven_9), .reset(undriven_13));
  D_Flip_Flop d_ff_4 (
    .clk(undriven), .D(undriven_2), .Q(d_ff_3_q), .Qn(d_ff_3_qn), .preset(undriven_9), .reset(undriven_13));
  or or_3 (or_3_out, and_5_out, and_6_out);
  D_Flip_Flop d_ff_5 (
    .clk(undriven_3), .D(undriven_4), .Q(d_ff_5_q), .Qn(d_ff_5_qn), .preset(undriven_10), .reset(undriven_14));
  D_Flip_Flop d_ff_6 (
    .clk(undriven_3), .D(undriven_4), .Q(d_ff_5_q), .Qn(d_ff_5_qn), .preset(undriven_10), .reset(undriven_14));
  or or_4 (or_4_out, and_7_out, and_8_out);
  D_Flip_Flop d_ff_7 (.D(or_5_out), .clk(CLOCK), .Q(Q[4]), .reset(CLEAR));  // open: Qn, preset
  or or_5 (or_5_out, and_9_out, and_10_out);
  D_Flip_Flop d_ff_8 (.D(or_6_out), .clk(CLOCK), .Q(Q[5]), .reset(CLEAR));  // open: Qn, preset
  or or_6 (or_6_out, and_11_out, and_12_out);
  D_Flip_Flop d_ff_9 (
    .clk(undriven_5), .D(undriven_6), .Q(d_ff_9_q), .Qn(d_ff_9_qn), .preset(undriven_11), .reset(undriven_15));
  D_Flip_Flop d_ff_10 (
    .clk(undriven_5), .D(undriven_6), .Q(d_ff_9_q), .Qn(d_ff_9_qn), .preset(undriven_11), .reset(undriven_15));
  or or_7 (or_7_out, and_13_out, and_14_out);
  D_Flip_Flop d_ff_11 (
    .clk(undriven_7), .D(undriven_8), .Q(d_ff_11_q), .Qn(d_ff_11_qn), .preset(undriven_12),
    .reset(undriven_16));
  D_Flip_Flop d_ff_12 (
    .clk(undriven_7), .D(undriven_8), .Q(d_ff_11_q), .Qn(d_ff_11_qn), .preset(undriven_12),
    .reset(undriven_16));
  or or_8 (or_8_out, and_15_out, and_16_out);
endmodule

module OCTALBUSTRANSCEIVER (
  input  ENA,
  input  [7:0] D,
  output [7:0] Q
);

  assign Q = ENA ? D : 8'bz;  // Controlled_Buffer controlled_buffer_1
endmodule

module ALU (
  input  [7:0] A,
  input  [7:0] B,
  input  SU,
  input  S2,
  input  S1,
  input  E0,
  output Carry,
  output [7:0] Result
);

  wire [7:0] adder8bit_1_out, and_1_out, mux4x1_1_y, or_1_out, xor_1_out;

  INVERTER inverter_1 (.Enable(SU));  // open: Input, Output
  ADDER8BIT adder8bit_1 (.A(A), .B(B), .Ci(SU), .Out(adder8bit_1_out), .Carry(Carry));
  assign and_1_out = A & B;  // AND_Gate and_1, 8 bits wide
  assign or_1_out = A | B;  // OR_Gate or_1, 8 bits wide
  assign xor_1_out = A ^ B;  // XOR_Gate xor_1, 8 bits wide
  MUX4X1 mux4x1_1 (
    .I0(adder8bit_1_out), .I1(and_1_out), .I2(or_1_out), .I3(xor_1_out), .S2(S2), .S1(S1), .Y(mux4x1_1_y));
  OCTALBUSTRANSCEIVER octalbustransceiver_1 (.D(mux4x1_1_y), .ENA(E0), .Q(Result));
endmodule

module ADDER8BIT (
  input  [7:0] A,
  input  [7:0] B,
  input  Ci,
  output [7:0] Out,
  output Carry
);

  wire adder1bit_1_co, adder1bit_2_co, adder1bit_3_co, adder1bit_4_co, adder1bit_5_co, adder1bit_6_co,
       adder1bit_7_co;

  ADDER1BIT adder1bit_1 (.Ci(Ci), .A(A[0]), .B(B[0]), .Q(Out[0]), .Co(adder1bit_1_co));
  ADDER1BIT adder1bit_2 (.Ci(adder1bit_3_co), .A(A[2]), .B(B[2]), .Q(Out[2]), .Co(adder1bit_2_co));
  ADDER1BIT adder1bit_3 (.Ci(adder1bit_1_co), .A(A[1]), .B(B[1]), .Q(Out[1]), .Co(adder1bit_3_co));
  ADDER1BIT adder1bit_4 (.Ci(adder1bit_2_co), .A(A[3]), .B(B[3]), .Q(Out[3]), .Co(adder1bit_4_co));
  ADDER1BIT adder1bit_5 (.Ci(adder1bit_4_co), .A(A[4]), .B(B[4]), .Q(Out[4]), .Co(adder1bit_5_co));
  ADDER1BIT adder1bit_6 (.Ci(adder1bit_5_co), .A(A[5]), .B(B[5]), .Q(Out[5]), .Co(adder1bit_6_co));
  ADDER1BIT adder1bit_7 (.Ci(adder1bit_6_co), .A(A[6]), .B(B[6]), .Q(Out[6]), .Co(adder1bit_7_co));
  ADDER1BIT adder1bit_8 (.Ci(adder1bit_7_co), .A(A[7]), .B(B[7]), .Q(Out[7]), .Co(Carry));
endmodule

module ADDER1BIT (
  input  Ci,
  input  A,
  input  B,
  output Q,
  output Co
);

  wire and_1_out, and_2_out, xor_1_out;

  xor xor_1 (xor_1_out, A, B);
  and and_1 (and_1_out, xor_1_out, Ci);
  and and_2 (and_2_out, A, B);
  xor xor_2 (Q, xor_1_out, Ci);
  or or_1 (Co, and_1_out, and_2_out);
endmodule

module INVERTER (
  input  Enable,
  input  [7:0] Input,
  output [7:0] Output
);

  xor xor_1 (Output[0], Input[0], Enable);
  xor xor_2 (Output[1], Input[1], Enable);
  xor xor_3 (Output[3], Input[3], Enable);
  xor xor_4 (Output[2], Input[2], Enable);
  xor xor_5 (Output[5], Input[5], Enable);
  xor xor_6 (Output[4], Input[4], Enable);
  xor xor_7 (Output[7], Input[7], Enable);
  xor xor_8 (Output[6], Input[6], Enable);
endmodule

module DECODER4TO16 (
  input  D,
  input  C,
  input  B,
  input  A,
  input  ENA,
  output Y0,
  output Y1,
  output Y2,
  output Y3,
  output Y4,
  output Y5,
  output Y6,
  output Y7,
  output Y8,
  output Y9,
  output Y10,
  output Y11,
  output Y12,
  output Y13,
  output Y14,
  output Y15
);

  wire not_1_out, not_2_out, not_3_out, not_4_out;

  not not_1 (not_1_out, D);
  not not_2 (not_2_out, C);
  not not_3 (not_3_out, B);
  not not_4 (not_4_out, A);
  and and_1 (Y0, not_1_out, not_2_out, not_3_out, not_4_out, ENA);
  and and_2 (Y1, D, not_2_out, not_3_out, not_4_out, ENA);
  and and_3 (Y2, not_1_out, C, not_3_out, not_4_out, ENA);
  and and_4 (Y3, D, C, not_3_out, not_4_out, ENA);
  and and_5 (Y4, not_1_out, not_2_out, B, not_4_out, ENA);
  and and_6 (Y5, D, not_2_out, B, not_4_out, ENA);
  and and_7 (Y6, not_1_out, C, B, not_4_out, ENA);
  and and_8 (Y7, D, C, B, not_4_out, ENA);
  and and_9 (Y8, not_1_out, not_2_out, not_3_out, A, ENA);
  and and_10 (Y9, D, not_2_out, not_3_out, A, ENA);
  and and_11 (Y10, not_1_out, C, not_3_out, A, ENA);
  and and_12 (Y11, D, C, not_3_out, A, ENA);
  and and_13 (Y12, not_1_out, not_2_out, B, A, ENA);
  and and_14 (Y13, D, not_2_out, B, A, ENA);
  and and_15 (Y14, not_1_out, C, B, A, ENA);
  and and_16 (Y15, D, C, B, A, ENA);
endmodule

module RAMREG8BIT (
  input  ENA,
  input  WR,
  input  [7:0] Data,
  input  RESET,
  output [7:0] Output
);

  wire and_1_out, and_2_out, not_1_out, or_1_out, or_2_out, or_3_out, or_4_out, or_5_out, or_6_out, or_7_out,
       or_8_out;
  wire [7:0] d_ff_8_q, octalbustransceiver_1_q;

  not not_1 (not_1_out, WR);
  and and_1 (and_1_out, ENA, WR);
  and and_2 (and_2_out, ENA, not_1_out);
  OCTALBUSTRANSCEIVER octalbustransceiver_1 (.D(Data), .ENA(and_1_out), .Q(octalbustransceiver_1_q));
  D_Flip_Flop d_ff_1 (.Q(d_ff_8_q[7]), .preset(octalbustransceiver_1_q[7]), .reset(or_1_out));  // open: D, clk, Qn
  or or_1 (or_1_out, ~octalbustransceiver_1_q[7], RESET);  // OR_Gate
  OCTALBUSTRANSCEIVER octalbustransceiver_2 (.D(d_ff_8_q), .ENA(and_2_out), .Q(Output));
  D_Flip_Flop d_ff_2 (.Q(d_ff_8_q[6]), .preset(octalbustransceiver_1_q[6]), .reset(or_2_out));  // open: D, clk, Qn
  or or_2 (or_2_out, ~octalbustransceiver_1_q[6], RESET);  // OR_Gate
  D_Flip_Flop d_ff_3 (.Q(d_ff_8_q[5]), .preset(octalbustransceiver_1_q[5]), .reset(or_3_out));  // open: D, clk, Qn
  or or_3 (or_3_out, ~octalbustransceiver_1_q[5], RESET);  // OR_Gate
  D_Flip_Flop d_ff_4 (.Q(d_ff_8_q[4]), .preset(octalbustransceiver_1_q[4]), .reset(or_4_out));  // open: D, clk, Qn
  or or_4 (or_4_out, ~octalbustransceiver_1_q[4], RESET);  // OR_Gate
  D_Flip_Flop d_ff_5 (.Q(d_ff_8_q[3]), .preset(octalbustransceiver_1_q[3]), .reset(or_5_out));  // open: D, clk, Qn
  or or_5 (or_5_out, ~octalbustransceiver_1_q[3], RESET);  // OR_Gate
  D_Flip_Flop d_ff_6 (.Q(d_ff_8_q[2]), .preset(octalbustransceiver_1_q[2]), .reset(or_6_out));  // open: D, clk, Qn
  or or_6 (or_6_out, ~octalbustransceiver_1_q[2], RESET);  // OR_Gate
  D_Flip_Flop d_ff_7 (.Q(d_ff_8_q[1]), .preset(octalbustransceiver_1_q[1]), .reset(or_7_out));  // open: D, clk, Qn
  or or_7 (or_7_out, ~octalbustransceiver_1_q[1], RESET);  // OR_Gate
  D_Flip_Flop d_ff_8 (.Q(d_ff_8_q[0]), .preset(octalbustransceiver_1_q[0]), .reset(or_8_out));  // open: D, clk, Qn
  or or_8 (or_8_out, ~octalbustransceiver_1_q[0], RESET);  // OR_Gate
endmodule

module RAM16BYTE (
  input  [3:0] A,
  input  RESET,
  input  [7:0] D,
  input  WR,
  input  CS,
  output [7:0] O
);

  wire decoder4to16_1_y0, decoder4to16_1_y1, decoder4to16_1_y2, decoder4to16_1_y3, decoder4to16_1_y4,
       decoder4to16_1_y5, decoder4to16_1_y6, decoder4to16_1_y7, decoder4to16_1_y8, decoder4to16_1_y9,
       decoder4to16_1_y10, decoder4to16_1_y11, decoder4to16_1_y12, decoder4to16_1_y13, decoder4to16_1_y14,
       decoder4to16_1_y15;
  wire [7:0] ramreg8bit_1_output;

  DECODER4TO16 decoder4to16_1 (
    .D(A[0]), .C(A[1]), .B(A[2]), .A(A[3]), .ENA(1'b1), .Y0(decoder4to16_1_y0), .Y1(decoder4to16_1_y1),
    .Y2(decoder4to16_1_y2), .Y3(decoder4to16_1_y3), .Y4(decoder4to16_1_y4), .Y5(decoder4to16_1_y5),
    .Y6(decoder4to16_1_y6), .Y7(decoder4to16_1_y7), .Y8(decoder4to16_1_y8), .Y9(decoder4to16_1_y9),
    .Y10(decoder4to16_1_y10), .Y11(decoder4to16_1_y11), .Y12(decoder4to16_1_y12), .Y13(decoder4to16_1_y13),
    .Y14(decoder4to16_1_y14), .Y15(decoder4to16_1_y15));
  RAMREG8BIT ramreg8bit_1 (.ENA(decoder4to16_1_y0), .WR(WR), .Data(D), .RESET(RESET), .Output(ramreg8bit_1_output));
  RAMREG8BIT ramreg8bit_2 (.ENA(decoder4to16_1_y8), .WR(WR), .Data(D), .RESET(RESET), .Output(ramreg8bit_1_output));
  RAMREG8BIT ramreg8bit_3 (.ENA(decoder4to16_1_y1), .WR(WR), .Data(D), .RESET(RESET), .Output(ramreg8bit_1_output));
  RAMREG8BIT ramreg8bit_4 (.ENA(decoder4to16_1_y9), .WR(WR), .Data(D), .RESET(RESET), .Output(ramreg8bit_1_output));
  RAMREG8BIT ramreg8bit_5 (.ENA(decoder4to16_1_y2), .WR(WR), .Data(D), .RESET(RESET), .Output(ramreg8bit_1_output));
  RAMREG8BIT ramreg8bit_6 (.ENA(decoder4to16_1_y10), .WR(WR), .Data(D), .RESET(RESET), .Output(ramreg8bit_1_output));
  RAMREG8BIT ramreg8bit_7 (.ENA(decoder4to16_1_y3), .WR(WR), .Data(D), .RESET(RESET), .Output(ramreg8bit_1_output));
  RAMREG8BIT ramreg8bit_8 (.ENA(decoder4to16_1_y11), .WR(WR), .Data(D), .RESET(RESET), .Output(ramreg8bit_1_output));
  RAMREG8BIT ramreg8bit_9 (.ENA(decoder4to16_1_y4), .WR(WR), .Data(D), .RESET(RESET), .Output(ramreg8bit_1_output));
  RAMREG8BIT ramreg8bit_10 (.ENA(decoder4to16_1_y12), .WR(WR), .Data(D), .RESET(RESET), .Output(ramreg8bit_1_output));
  RAMREG8BIT ramreg8bit_11 (.ENA(decoder4to16_1_y5), .WR(WR), .Data(D), .RESET(RESET), .Output(ramreg8bit_1_output));
  RAMREG8BIT ramreg8bit_12 (.ENA(decoder4to16_1_y13), .WR(WR), .Data(D), .RESET(RESET), .Output(ramreg8bit_1_output));
  RAMREG8BIT ramreg8bit_13 (.ENA(decoder4to16_1_y6), .WR(WR), .Data(D), .RESET(RESET), .Output(ramreg8bit_1_output));
  RAMREG8BIT ramreg8bit_14 (.ENA(decoder4to16_1_y14), .WR(WR), .Data(D), .RESET(RESET), .Output(ramreg8bit_1_output));
  RAMREG8BIT ramreg8bit_15 (.ENA(decoder4to16_1_y7), .WR(WR), .Data(D), .RESET(RESET), .Output(ramreg8bit_1_output));
  RAMREG8BIT ramreg8bit_16 (.ENA(decoder4to16_1_y15), .WR(WR), .Data(D), .RESET(RESET), .Output(ramreg8bit_1_output));
  OCTALBUSTRANSCEIVER octalbustransceiver_1 (.D(ramreg8bit_1_output), .ENA(CS), .Q(O));
endmodule

module MUX4X1 (
  input  S2,
  input  S1,
  input  [7:0] I0,
  input  [7:0] I1,
  input  [7:0] I2,
  input  [7:0] I3,
  output [7:0] Y
);

  wire not_1_out, not_2_out;
  wire [7:0] and_1_out, and_2_out, and_3_out, and_4_out, bit_extender_1_out, bit_extender_2_out,
       bit_extender_3_out, bit_extender_4_out;

  not not_1 (not_1_out, S2);
  assign bit_extender_1_out = {{7{not_1_out}}, not_1_out};  // Bit_Extender bit_extender_1
  assign bit_extender_2_out = {{7{S2}}, S2};  // Bit_Extender bit_extender_2
  not not_2 (not_2_out, S1);
  assign bit_extender_3_out = {{7{not_2_out}}, not_2_out};  // Bit_Extender bit_extender_3
  assign bit_extender_4_out = {{7{S1}}, S1};  // Bit_Extender bit_extender_4
  assign and_1_out = bit_extender_3_out & I0 & bit_extender_1_out;  // AND_Gate and_1, 8 bits wide
  assign and_2_out = bit_extender_4_out & I1 & bit_extender_1_out;  // AND_Gate and_2, 8 bits wide
  assign and_3_out = bit_extender_3_out & I2 & bit_extender_2_out;  // AND_Gate and_3, 8 bits wide
  assign and_4_out = bit_extender_4_out & I3 & bit_extender_2_out;  // AND_Gate and_4, 8 bits wide
  assign Y = and_1_out | and_2_out | and_3_out | and_4_out;  // OR_Gate or_1, 8 bits wide
endmodule

module MUX2X1 (
  input  [3:0] A,
  input  [3:0] B,
  input  Select,
  output [3:0] Out
);

  wire [3:0] and_1_out, and_2_out, bit_extender_1_out, not_1_out;

  assign bit_extender_1_out = {{3{Select}}, Select};  // Bit_Extender bit_extender_1
  assign not_1_out = ~bit_extender_1_out;  // NOT_Gate not_1, 4 bits wide
  assign and_1_out = A & bit_extender_1_out;  // AND_Gate and_1, 4 bits wide
  assign and_2_out = B & not_1_out;  // AND_Gate and_2, 4 bits wide
  assign Out = and_1_out | and_2_out;  // OR_Gate or_1, 4 bits wide
endmodule

module MEMREG4BIT (
  input  CLEAR,
  input  LOAD,
  input  [3:0] D,
  input  CLOCK,
  output [3:0] Q
);

  wire and_1_out, and_2_out, and_3_out, and_4_out, and_5_out, and_6_out, and_7_out, and_8_out, d_ff_3_q,
       d_ff_3_qn, d_ff_5_q, d_ff_5_qn, not_1_out, not_2_out, not_3_out, not_4_out, or_1_out, or_2_out,
       or_3_out, or_4_out, undriven, undriven_2, undriven_3, undriven_4, undriven_5, undriven_6, undriven_7,
       undriven_8;

  not not_1 (not_1_out, LOAD);
  not not_2 (not_2_out, LOAD);
  not not_3 (not_3_out, LOAD);
  not not_4 (not_4_out, LOAD);
  and and_1 (and_1_out, Q[0], not_1_out);
  and and_2 (and_2_out, LOAD, D[0]);
  and and_3 (and_3_out, Q[1], not_2_out);
  and and_4 (and_4_out, LOAD, D[1]);
  and and_5 (and_5_out, Q[2], not_3_out);
  and and_6 (and_6_out, LOAD, D[2]);
  and and_7 (and_7_out, Q[3], not_4_out);
  and and_8 (and_8_out, LOAD, D[3]);
  D_Flip_Flop d_ff_1 (.D(or_1_out), .clk(CLOCK), .Q(Q[0]), .reset(CLEAR));  // open: Qn, preset
  or or_1 (or_1_out, and_1_out, and_2_out);
  D_Flip_Flop d_ff_2 (.D(or_2_out), .clk(CLOCK), .Q(Q[1]), .reset(CLEAR));  // open: Qn, preset
  or or_2 (or_2_out, and_3_out, and_4_out);
  D_Flip_Flop d_ff_3 (
    .clk(undriven), .D(undriven_2), .Q(d_ff_3_q), .Qn(d_ff_3_qn), .preset(undriven_5), .reset(undriven_7));
  D_Flip_Flop d_ff_4 (
    .clk(undriven), .D(undriven_2), .Q(d_ff_3_q), .Qn(d_ff_3_qn), .preset(undriven_5), .reset(undriven_7));
  or or_3 (or_3_out, and_5_out, and_6_out);
  D_Flip_Flop d_ff_5 (
    .clk(undriven_3), .D(undriven_4), .Q(d_ff_5_q), .Qn(d_ff_5_qn), .preset(undriven_6), .reset(undriven_8));
  D_Flip_Flop d_ff_6 (
    .clk(undriven_3), .D(undriven_4), .Q(d_ff_5_q), .Qn(d_ff_5_qn), .preset(undriven_6), .reset(undriven_8));
  or or_4 (or_4_out, and_7_out, and_8_out);
endmodule

module COUNTER4BIT (
  input  D0,
  input  D1,
  input  D2,
  input  D3,
  input  LOAD,
  input  ENA,
  input  CLK,
  input  RESET,
  output Q0,
  output Q1,
  output Q2,
  output Q3
);

  wire and_1_out, and_2_out, and_3_out, and_4_out, and_5_out, and_6_out, and_7_out, or_1_out, or_2_out,
       or_3_out, or_4_out;

  and and_1 (and_1_out, LOAD, ~D0);  // AND_Gate
  COUNTER1BIT counter1bit_1 (.ENA(ENA), .CLK(CLK), .LOAD(LOAD), .DATA(D0), .RESET(or_1_out), .Q(Q0));
  or or_1 (or_1_out, and_1_out, RESET);
  COUNTER1BIT counter1bit_2 (.ENA(and_2_out), .CLK(CLK), .LOAD(LOAD), .DATA(D1), .RESET(or_2_out), .Q(Q1));
  and and_2 (and_2_out, Q0, ENA);
  or or_2 (or_2_out, and_3_out, RESET);
  and and_3 (and_3_out, LOAD, ~D1);  // AND_Gate
  and and_4 (and_4_out, Q1, and_2_out);
  or or_3 (or_3_out, and_5_out, RESET);
  and and_5 (and_5_out, LOAD, ~D2);  // AND_Gate
  COUNTER1BIT counter1bit_3 (.ENA(and_4_out), .CLK(CLK), .LOAD(LOAD), .DATA(D2), .RESET(or_3_out), .Q(Q2));
  and and_6 (and_6_out, Q2, and_4_out);
  and and_7 (and_7_out, LOAD, ~D3);  // AND_Gate
  COUNTER1BIT counter1bit_4 (.ENA(and_6_out), .CLK(CLK), .LOAD(LOAD), .DATA(D3), .RESET(or_4_out), .Q(Q3));
  or or_4 (or_4_out, and_7_out, RESET);
endmodule

module COUNTER1BIT (
  input  LOAD,
  input  DATA,
  input  ENA,
  input  CLK,
  input  RESET,
  output Q
);

  wire and_1_out, and_2_out, and_3_out, j_k_ff_1_qn;

  and and_1 (and_1_out, j_k_ff_1_qn, ENA);
  and and_2 (and_2_out, ENA, Q);
  and and_3 (and_3_out, LOAD, DATA);
  J_K_Flip_Flop j_k_ff_1 (
    .J(and_1_out), .K(and_2_out), .clk(CLK), .Q(Q), .Qn(j_k_ff_1_qn), .preset(and_3_out), .reset(RESET));
endmodule

module QUATERNARYTRANSCEIVER (
  input  ENA,
  input  [3:0] D,
  output [3:0] Q
);

  assign Q = ENA ? D : 4'bz;  // Controlled_Buffer controlled_buffer_1
endmodule
