// Logisim project INSTRUCTION_ROM.circ as structural Verilog: 1 circuit, main circuit INSTRUCTION_ROM
module INSTRUCTION_ROM (
  input  S0,
  input  S1,
  input  S2,
  input  IR0,
  input  IR1,
  input  IR2,
  input  IR3,
  output out_8,
  output JMP,
  output CO,
  output CE,
  output DISPLAY,
  output BOUT,
  output BIN,
  output SIGNED,
  output S1_2,
  output S2_2,
  output SU,
  output E0,
  output AOUT,
  output AIN,
  output IRIN,
  output IRLOAD,
  output WR,
  output CS,
  output MI,
  output HLT
);

  ROM #(.addrWidth(7), .dataWidth(20)) rom_1 (
    .addr({IR3, IR2, IR1, IR0, S2, S1, S0}),
    .data({HLT, MI, CS, WR, IRLOAD, IRIN, AIN, AOUT, E0, SU, S2_2, S1_2, SIGNED, BIN, BOUT, DISPLAY, CE, CO, JMP, out_8}));

  // Notes on the sheet:
  //   contents of rom_1 (hex, n*v repeats v):
  //   40004 28008 6*0 40004 28008 44000 22000 4*0 40004 28008 44000 20040 2800 3*0 40004 28008 44000 20040
  //   2c00 3*0 40004 28008 6*0 40004 28008 6*0 40004 28008 6*0 40004 28008 6*0 40004 28008 6*0 40004 28008
  //   6*0 40004 28008 6*0 40004 28008 6*0 40004 28008 6*0 40004 28008 6*0 40004 28008 1010 7*0 80000
endmodule
